# Fritzing sketch AM2302MiniBreadboard (saved by Fritzing 0.9.2b)
breadboards: 1

parts:
  AM2302 = Humidity and Temperature Sensor RHT03
  Arduino1 = Arduino Uno (Rev3)

nets:
  N1: AM2302.Data-signal, Arduino1.D2
  N2: AM2302.GND_1, Arduino1.GND

notes:
  Arduino Uno + AM2302 Sensor
  Derek Erb - 31/01/2013
  about.me/derekerb
  derek.erb@gmail.com
  AM2302 +5v power to Arduino 5v
  AM2302 Data to Arduino Pin 2 (or 3)
  AM2302 Supplementary ground to Arduino GND
  AM2302 Principal ground to Arduino GND
  AM2302 Left to right
  Sticker / Label facing up
